// Logisim project 1970cpu.circ as structural Verilog: 3 circuits, main circuit main
module main (
  input  reset
);

  wire clock_1_out, jump, we;
  wire [2:0] addy1, addy2, addy3, regs_1_porta;
  wire [3:0] alu_1_alu_out, multiplexer_2_out, regs_1_portb;
  wire [3:3] dout, regs_1_porta_2;
  wire [7:0] counter_1_q, rom_2_data;
  wire [7:7] jumpto;
  wire [15:11] rom_1_data;

  Clock clock_1 (.out(clock_1_out));
  Counter counter_1 (
    .clr(reset), .load(jump), .clk(clock_1_out), .D({jumpto[7], addy1, dout[3], addy2}), .Q(counter_1_q));  // open: up, count, carry
  TTY tty_1 (.data({regs_1_porta, regs_1_portb}), .clk(clock_1_out), .we(we), .clr(reset));
  ROM #(.dataWidth(16), .misaligned("true")) rom_1 (
    .addr(counter_1_q), .data({rom_1_data, addy3, jumpto[7], addy1, dout[3], addy2}));
  alu alu_1 (.A({regs_1_porta_2[3], regs_1_porta}), .B(regs_1_portb), .S(rom_2_data[7:4]), .ALU_out(alu_1_alu_out));
  regs regs_1 (
    .WE(rom_2_data[0]), .WAddr(addy3), .Data_in(multiplexer_2_out), .RAddrB(addy2), .RAddrA(addy1),
    .PortB(regs_1_portb), .PortA({regs_1_porta_2[3], regs_1_porta}));
  Multiplexer #(.select(4)) multiplexer_1 (
    .in0(1'b0), .in1(1'b0), .in2(1'b0), .in3(1'b0), .in4(1'b0), .in5(1'b0), .in6(1'b0), .in7(1'b0),
    .in8(1'b0), .in9(1'b0), .in10(1'b0), .in11(1'b0), .in12(1'b0), .in13(1'b0), .in14(1'b1), .in15(1'b0),
    .out(jump), .sel(rom_1_data[15:12]));
  ROM #(.addrWidth(4)) rom_2 (.addr(rom_1_data[15:12]), .data({rom_2_data[7:2], we, rom_2_data[0]}));
  Multiplexer #(.select(2), .width(4)) multiplexer_2 (
    .in0({dout[3], addy2}), .in1(alu_1_alu_out), .in2({regs_1_porta_2[3], regs_1_porta}),
    .out(multiplexer_2_out), .sel(rom_2_data[3:2]));  // open: in3

  // Other names for the same wires on the sheet: dout[2:0] = addy2; jumpto[6:0] = {addy1, dout[3], addy2}; r = reset

  // Notes on the sheet:
  //   MSB 1 = load into register
  //   MSB 2 = copy to a different register
  //   MSB 3 = write something on tty
  //   MSB 4-6 are XOR, AND, OR functions 
  //   MSB 8-9 is shift left and right
  //   MSB E = jump to specific part
  //   MSB 7/f is add or subtract
  //   MSB a/c is multiply or divide
  //   MSB D = exponent
  //   MBS B = personal comparator   produces ascii code for the result of operands
  //   contents of rom_1 (hex, n*v repeats v):
  //   1003 1106 3010 1002 1207 3020 1005 3010 1001 3010 1004 3020 1005 3010 1004 3010 1300 1402 3043 1002
  //   3010 1009 3020 3043 100a 3010 100f 3010 1008 3010 100e 3010 3043 3022 1005 3010 100e 3010 1004 3010
  //   3020 100a 1100 3010 4*0 1005 1103 3010 100b 1102 3010 1103 3011 100d 3010 1505 1603 7756 3017 100a
  //   1100 3010 1005 1103 3010 100d 1102 3010 1103 3011 100d 3010 f751 3017 100a 1100 3010 1103 3011 1202
  //   3020 3011 100d 3010 a711 3017 100a 1100 3010 1001 1103 3010 1002 3010 100f 1102 3010 1103 3011 100d
  //   3010 120c 1303 c723 3017 100a 1100 3010 1002 1103 3010 100e 1205 3020 3011 100d 3010 1002 d710 3017
  //   100a 1100 3010 1003 1106 3010 100f 1106 3010 1000 1107 3010 1009 3010 100a 1103 3010 2070 3010 88*0
  //   1008 1100 6*3010 100c 3010 15*0 e000
  //   bit 1 is which register
  //   bit 1 is where it goes
  //   use reverse hex of ascii code for it
  //   bit 1 is the register its loaded in
  //   bit 1 is where it goes
  //   bits 1-3 are hexadecimal for address
  //   bit 1 is the register its loaded in
  //   This machine code:
  //   bit 2 is which reg it takes
  //   bits 2-3 are the operands
  //   bit 2 is the first number
  //   contents of rom_2 (hex, n*v repeats v):
  //   0 1 9 2 95 5 15 25 35 b5 45 55 65 75 0 a5
  //   bit 3 is what number
  //   bit 3 is which reg it takes
  //   bit 3 is the number applied to formula
endmodule

module regs (
  input  WE,
  input  [2:0] WAddr,
  input  [3:0] Data_in,
  input  [2:0] RAddrB,
  input  [2:0] RAddrA,
  output [3:0] PortB,
  output [3:0] PortA
);

  wire clk, wr0, wr1, wr2, wr3, wr4, wr5, wr6, wr7;
  wire [3:0] fourbitreg_1_dout, fourbitreg_2_dout, fourbitreg_3_dout, fourbitreg_4_dout, fourbitreg_5_dout,
       fourbitreg_6_dout, fourbitreg_7_dout, fourbitreg_8_dout;

  Clock clock_1 (.out(clk));
  Decoder #(.select(3)) decoder_1 (
    .out0(wr0), .out1(wr1), .out2(wr2), .out3(wr3), .out4(wr4), .out5(wr5), .out6(wr6), .out7(wr7),
    .sel(WAddr), .en(WE));
  fourbitreg fourbitreg_1 (.Din(Data_in), .Write(wr0), .Clk(clk), .Dout(fourbitreg_1_dout));
  fourbitreg fourbitreg_2 (.Din(Data_in), .Write(wr1), .Clk(clk), .Dout(fourbitreg_2_dout));
  fourbitreg fourbitreg_3 (.Din(Data_in), .Write(wr2), .Clk(clk), .Dout(fourbitreg_3_dout));
  fourbitreg fourbitreg_4 (.Din(Data_in), .Write(wr3), .Clk(clk), .Dout(fourbitreg_4_dout));
  fourbitreg fourbitreg_5 (.Din(Data_in), .Write(wr4), .Clk(clk), .Dout(fourbitreg_5_dout));
  fourbitreg fourbitreg_6 (.Din(Data_in), .Write(wr5), .Clk(clk), .Dout(fourbitreg_6_dout));
  fourbitreg fourbitreg_7 (.Din(Data_in), .Write(wr6), .Clk(clk), .Dout(fourbitreg_7_dout));
  fourbitreg fourbitreg_8 (.Din(Data_in), .Write(wr7), .Clk(clk), .Dout(fourbitreg_8_dout));
  Multiplexer #(.select(3), .width(4)) multiplexer_1 (
    .in0(fourbitreg_1_dout), .in1(fourbitreg_2_dout), .in2(fourbitreg_3_dout), .in3(fourbitreg_4_dout),
    .in4(fourbitreg_5_dout), .in5(fourbitreg_6_dout), .in6(fourbitreg_7_dout), .in7(fourbitreg_8_dout),
    .out(PortA), .sel(RAddrA));
  Multiplexer #(.select(3), .width(4)) multiplexer_2 (
    .in0(fourbitreg_1_dout), .in1(fourbitreg_2_dout), .in2(fourbitreg_3_dout), .in3(fourbitreg_4_dout),
    .in4(fourbitreg_5_dout), .in5(fourbitreg_6_dout), .in6(fourbitreg_7_dout), .in7(fourbitreg_8_dout),
    .out(PortB), .sel(RAddrB));

  // Notes on the sheet:
  //   john wendt
endmodule

module fourbitreg (
  input  [3:0] Din,
  input  Write,
  input  Clk,
  output [3:0] Dout
);

  wire multiplexer_1_out, multiplexer_2_out, multiplexer_3_out, multiplexer_4_out;

  Multiplexer multiplexer_1 (.in0(Dout[0]), .in1(Din[0]), .out(multiplexer_1_out), .sel(Write));
  Multiplexer multiplexer_2 (.in0(Dout[1]), .in1(Din[1]), .out(multiplexer_2_out), .sel(Write));
  Multiplexer multiplexer_3 (.in0(Dout[2]), .in1(Din[2]), .out(multiplexer_3_out), .sel(Write));
  Multiplexer multiplexer_4 (.in0(Dout[3]), .in1(Din[3]), .out(multiplexer_4_out), .sel(Write));
  D_Flip_Flop d_ff_1 (.D(multiplexer_1_out), .clk(Clk), .Q(Dout[0]));  // open: Qn, preset, reset
  D_Flip_Flop d_ff_2 (.D(multiplexer_2_out), .clk(Clk), .Q(Dout[1]));  // open: Qn, preset, reset
  D_Flip_Flop d_ff_3 (.D(multiplexer_3_out), .clk(Clk), .Q(Dout[2]));  // open: Qn, preset, reset
  D_Flip_Flop d_ff_4 (.D(multiplexer_4_out), .clk(Clk), .Q(Dout[3]));  // open: Qn, preset, reset

  // Other names for the same wires on the sheet: hold0 = Dout[0]; hold1 = Dout[1]; hold2 = Dout[2]; hold3 = Dout[3];
  //   s = Write

  // Notes on the sheet:
  //   john wendt
endmodule
