// Logisim project Lab6_ALU.circ as structural Verilog: 9 circuits, main circuit alu
module Full_Adder (
  input  A,
  input  B,
  input  Cin,
  output S,
  output Cout
);

  wire and_1_out, and_2_out, and_3_out;

  xor xor_1 (S, A, B, Cin);
  and and_1 (and_1_out, A, B);
  and and_2 (and_2_out, B, Cin);
  and and_3 (and_3_out, A, Cin);
  or or_1 (Cout, and_1_out, and_2_out, and_3_out);
endmodule

module OR_4bit (
  input  [3:0] A,
  input  do_xor,
  input  [3:0] B,
  output [3:0] OR4
);

  wire [3:0] or_1_out, xor_1_out;

  assign or_1_out = A | B;  // OR_Gate or_1, 4 bits wide
  assign xor_1_out = A ^ B;  // XOR_Gate xor_1, 4 bits wide
  Multiplexer #(.width(4)) multiplexer_1 (.in0(or_1_out), .in1(xor_1_out), .out(OR4), .sel(do_xor));
endmodule

module Add_4bit (
  input  [3:0] A,
  input  addOrSub,
  input  [3:0] B,
  output [3:0] ADD4
);

  wire c0, c1, c2;
  wire [3:0] or_4bit_1_or4;

  OR_4bit or_4bit_1 (.A({4{addOrSub}}), .do_xor(1'b1), .B(B), .OR4(or_4bit_1_or4));
  Full_Adder full_adder_1 (.A(A[0]), .B(or_4bit_1_or4[0]), .Cin(addOrSub), .S(ADD4[0]), .Cout(c0));
  Full_Adder full_adder_2 (.A(A[1]), .B(or_4bit_1_or4[1]), .Cin(c0), .S(ADD4[1]), .Cout(c1));
  Full_Adder full_adder_3 (.A(or_4bit_1_or4[2]), .B(A[2]), .Cin(c1), .S(ADD4[2]), .Cout(c2));
  Full_Adder full_adder_4 (.A(A[3]), .B(or_4bit_1_or4[3]), .Cin(c2), .S(ADD4[3]));  // open: Cout

  // Other names for the same wires on the sheet: msb = addOrSub

  // Notes on the sheet:
  //   john wendt
endmodule

module alu (
  input  [3:0] A,
  input  [3:0] B,
  input  [3:0] S,
  output [3:0] ALU_out
);

  wire [3:0] add_4bit_1_add4, and_1_out, divide_floor_1_f, exponent_1_f, mult_1_f, or_4bit_1_or4,
       personal_comparator_1_f, shift_1_f;

  assign and_1_out = A & B;  // AND_Gate and_1, 4 bits wide
  OR_4bit or_4bit_1 (.A(A), .do_xor(S[3]), .B(B), .OR4(or_4bit_1_or4));
  Add_4bit add_4bit_1 (.A(A), .addOrSub(S[3]), .B(B), .ADD4(add_4bit_1_add4));
  shift shift_1 (.put(A), .leftOrRight(S[3]), .F(shift_1_f));
  MULT mult_1 (.A(A), .B(B), .F(mult_1_f));
  personal_comparator personal_comparator_1 (.A(B), .B(A), .F(personal_comparator_1_f));
  divide_floor divide_floor_1 (.A(A), .B(B), .F(divide_floor_1_f));
  exponent exponent_1 (.A(B), .B(A), .F(exponent_1_f));
  Multiplexer #(.select(3), .width(4)) multiplexer_1 (
    .in0(and_1_out), .in1(or_4bit_1_or4), .in2(add_4bit_1_add4), .in3(shift_1_f), .in4(mult_1_f),
    .in5(personal_comparator_1_f), .in6(divide_floor_1_f), .in7(exponent_1_f), .out(ALU_out), .sel(S[2:0]));

  // Other names for the same wires on the sheet: twofunc = S[3]

  // Notes on the sheet:
  //   AND_4bit
endmodule

module MULT (
  input  [3:0] A,
  input  [3:0] B,
  output [3:0] F
);

  wire [3:0] add_4bit_1_add4, add_4bit_3_add4, and_1_out, and_2_out, and_3_out, and_4_out, shift_1_f,
       shift_2_f, shift_3_f, shift_4_f, shift_5_f, shift_6_f;

  assign and_1_out = {4{A[0]}} & B;  // AND_Gate and_1, 4 bits wide
  assign and_2_out = {4{A[1]}} & B;  // AND_Gate and_2, 4 bits wide
  assign and_3_out = {4{A[2]}} & B;  // AND_Gate and_3, 4 bits wide
  assign and_4_out = {4{A[3]}} & B;  // AND_Gate and_4, 4 bits wide
  shift shift_1 (.put(and_2_out), .F(shift_1_f));  // open: leftOrRight
  shift shift_2 (.put(and_3_out), .F(shift_2_f));  // open: leftOrRight
  shift shift_3 (.put(and_4_out), .F(shift_3_f));  // open: leftOrRight
  Add_4bit add_4bit_1 (.A(and_1_out), .B(shift_1_f), .ADD4(add_4bit_1_add4));  // open: addOrSub
  shift shift_4 (.put(shift_2_f), .F(shift_4_f));  // open: leftOrRight
  shift shift_5 (.put(shift_3_f), .F(shift_5_f));  // open: leftOrRight
  shift shift_6 (.put(shift_5_f), .F(shift_6_f));  // open: leftOrRight
  Add_4bit add_4bit_2 (.A(add_4bit_1_add4), .B(add_4bit_3_add4), .ADD4(F));  // open: addOrSub
  Add_4bit add_4bit_3 (.A(shift_4_f), .B(shift_6_f), .ADD4(add_4bit_3_add4));  // open: addOrSub
endmodule

module shift (
  input  [3:0] put,
  input  leftOrRight,
  output [3:0] F
);

  Multiplexer #(.width(4)) multiplexer_1 (.in0({put[2:0], 1'b0}), .in1({1'b0, put[3:1]}), .out(F), .sel(leftOrRight));
endmodule

module personal_comparator (
  input  [3:0] A,
  input  [3:0] B,
  output [3:0] F
);

  wire and_1_out, and_2_out, and_3_out, and_4_out, and_5_out, and_6_out, and_7_out, and_8_out, not_1_out,
       not_2_out, not_3_out, not_4_out, not_5_out, not_6_out, not_7_out, not_8_out, xnor_1_out, xnor_2_out,
       xnor_3_out, xnor_4_out;
  wire [2:0] or_1_out;

  not not_1 (not_1_out, B[3]);
  not not_2 (not_2_out, B[2]);
  not not_3 (not_3_out, B[1]);
  not not_4 (not_4_out, B[0]);
  xnor xnor_1 (xnor_1_out, A[3], B[3]);
  xnor xnor_2 (xnor_2_out, A[2], B[2]);
  xnor xnor_3 (xnor_3_out, A[1], B[1]);
  xnor xnor_4 (xnor_4_out, A[0], B[0]);
  not not_5 (not_5_out, A[0]);
  not not_6 (not_6_out, A[1]);
  not not_7 (not_7_out, A[2]);
  not not_8 (not_8_out, A[3]);
  and and_1 (and_1_out, A[3], not_1_out);
  and and_2 (and_2_out, A[2], not_2_out, xnor_1_out);
  and and_3 (and_3_out, A[1], not_3_out, xnor_1_out, xnor_2_out);
  and and_4 (and_4_out, A[0], not_4_out, xnor_1_out, xnor_2_out, xnor_3_out);
  and and_5 (and_5_out, xnor_3_out, xnor_2_out, xnor_1_out, not_5_out, B[0]);
  and and_6 (and_6_out, xnor_2_out, xnor_1_out, not_6_out, B[1]);
  and and_7 (and_7_out, xnor_1_out, not_7_out, B[2]);
  and and_8 (and_8_out, not_8_out, B[3]);
  or or_1 (or_1_out[0], and_1_out, and_2_out, and_3_out, and_4_out);
  and and_9 (or_1_out[1], xnor_1_out, xnor_2_out, xnor_3_out, xnor_4_out);
  or or_2 (or_1_out[2], and_5_out, and_6_out, and_7_out, and_8_out);
  Multiplexer #(.select(3), .width(4)) multiplexer_1 (
    .in1(4'b1110), .in2(4'b1101), .in4(4'b1100), .out(F), .sel(or_1_out));  // open: in0, in3, in5, in6, in7

  // Notes on the sheet:
  //   greater 3e
  //   equal 3d
  //   lesser 3c
endmodule

module divide_floor (
  input  [3:0] A,
  input  [3:0] B,
  output [3:0] F
);

  wire c1, c2, c3, c4, c5, c6, c7, c8, c9, c10, c11, c12, c13, c14, c15, comparator_1_lt, comparator_2_lt,
       comparator_3_lt, comparator_4_lt, comparator_5_lt, comparator_6_lt, comparator_7_lt, comparator_8_lt,
       comparator_9_lt, comparator_10_lt, comparator_11_lt, comparator_12_lt, comparator_13_lt,
       comparator_14_lt, comparator_15_lt, comparator_16_lt, comparator_17_eq, not_16_out;
  wire [3:0] a1, a2, a3, a4, a5, a6, a7, a8, a9, a10, a11, a12, a13, a14, a15, add_4bit_1_add4,
       add_4bit_2_add4, add_4bit_3_add4, add_4bit_4_add4, add_4bit_5_add4, add_4bit_6_add4, add_4bit_7_add4,
       add_4bit_8_add4, add_4bit_9_add4, add_4bit_10_add4, add_4bit_11_add4, add_4bit_12_add4,
       add_4bit_13_add4, add_4bit_14_add4, add_4bit_15_add4, add_4bit_16_add4, add_4bit_17_add4,
       add_4bit_18_add4, add_4bit_19_add4, add_4bit_20_add4, add_4bit_21_add4, add_4bit_22_add4,
       add_4bit_23_add4, add_4bit_24_add4, add_4bit_25_add4, add_4bit_26_add4, add_4bit_27_add4,
       add_4bit_28_add4, add_4bit_29_add4, add_4bit_30_add4, add_4bit_31_add4, and_16_out,
       bit_extender_1_out, bit_extender_2_out, bit_extender_3_out, bit_extender_4_out, bit_extender_5_out,
       bit_extender_6_out, bit_extender_7_out, bit_extender_8_out, bit_extender_9_out, bit_extender_10_out,
       bit_extender_11_out, bit_extender_12_out, bit_extender_13_out, bit_extender_14_out,
       bit_extender_15_out, bit_extender_16_out;

  Comparator #(.mode("unsigned"), .width(4)) comparator_1 (.a(A), .b(B), .lt(comparator_1_lt));  // open: gt, eq
  Comparator #(.mode("unsigned"), .width(4)) comparator_2 (.a(a1), .b(B), .lt(comparator_2_lt));  // open: gt, eq
  Comparator #(.mode("unsigned"), .width(4)) comparator_3 (.a(a2), .b(B), .lt(comparator_3_lt));  // open: gt, eq
  Comparator #(.mode("unsigned"), .width(4)) comparator_4 (.a(a3), .b(B), .lt(comparator_4_lt));  // open: gt, eq
  Comparator #(.mode("unsigned"), .width(4)) comparator_5 (.a(a4), .b(B), .lt(comparator_5_lt));  // open: gt, eq
  Comparator #(.mode("unsigned"), .width(4)) comparator_6 (.a(a5), .b(B), .lt(comparator_6_lt));  // open: gt, eq
  Comparator #(.mode("unsigned"), .width(4)) comparator_7 (.a(a6), .b(B), .lt(comparator_7_lt));  // open: gt, eq
  Comparator #(.mode("unsigned"), .width(4)) comparator_8 (.a(a7), .b(B), .lt(comparator_8_lt));  // open: gt, eq
  not not_1 (c1, comparator_1_lt);
  not not_2 (c2, comparator_2_lt);
  not not_3 (c3, comparator_3_lt);
  not not_4 (c4, comparator_4_lt);
  not not_5 (c5, comparator_5_lt);
  not not_6 (c6, comparator_6_lt);
  not not_7 (c7, comparator_7_lt);
  not not_8 (c8, comparator_8_lt);
  assign bit_extender_1_out = {{3{c1}}, c1};  // Bit_Extender bit_extender_1
  assign a1 = bit_extender_1_out & add_4bit_1_add4;  // AND_Gate and_1, 4 bits wide
  Add_4bit add_4bit_1 (.A(A), .addOrSub(1'b1), .B(B), .ADD4(add_4bit_1_add4));
  assign bit_extender_2_out = {{3{c2}}, c2};  // Bit_Extender bit_extender_2
  assign a2 = bit_extender_2_out & add_4bit_2_add4;  // AND_Gate and_2, 4 bits wide
  Add_4bit add_4bit_2 (.A(a1), .addOrSub(1'b1), .B(B), .ADD4(add_4bit_2_add4));
  assign bit_extender_3_out = {{3{c3}}, c3};  // Bit_Extender bit_extender_3
  assign a3 = bit_extender_3_out & add_4bit_3_add4;  // AND_Gate and_3, 4 bits wide
  Add_4bit add_4bit_3 (.A(a2), .addOrSub(1'b1), .B(B), .ADD4(add_4bit_3_add4));
  assign bit_extender_4_out = {{3{c4}}, c4};  // Bit_Extender bit_extender_4
  assign a4 = bit_extender_4_out & add_4bit_4_add4;  // AND_Gate and_4, 4 bits wide
  Add_4bit add_4bit_4 (.A(a3), .addOrSub(1'b1), .B(B), .ADD4(add_4bit_4_add4));
  assign bit_extender_5_out = {{3{c5}}, c5};  // Bit_Extender bit_extender_5
  assign a5 = bit_extender_5_out & add_4bit_5_add4;  // AND_Gate and_5, 4 bits wide
  Add_4bit add_4bit_5 (.A(a4), .addOrSub(1'b1), .B(B), .ADD4(add_4bit_5_add4));
  assign bit_extender_6_out = {{3{c6}}, c6};  // Bit_Extender bit_extender_6
  assign a6 = bit_extender_6_out & add_4bit_6_add4;  // AND_Gate and_6, 4 bits wide
  Add_4bit add_4bit_6 (.A(a5), .addOrSub(1'b1), .B(B), .ADD4(add_4bit_6_add4));
  assign bit_extender_7_out = {{3{c7}}, c7};  // Bit_Extender bit_extender_7
  assign a7 = bit_extender_7_out & add_4bit_7_add4;  // AND_Gate and_7, 4 bits wide
  Add_4bit add_4bit_7 (.A(a6), .addOrSub(1'b1), .B(B), .ADD4(add_4bit_7_add4));
  assign bit_extender_8_out = {{3{c8}}, c8};  // Bit_Extender bit_extender_8
  assign a8 = bit_extender_8_out & add_4bit_8_add4;  // AND_Gate and_8, 4 bits wide
  Add_4bit add_4bit_8 (.A(a7), .addOrSub(1'b1), .B(B), .ADD4(add_4bit_8_add4));
  Add_4bit add_4bit_9 (.A({3'b000, c1}), .B({3'b000, c2}), .ADD4(add_4bit_9_add4));  // open: addOrSub
  Add_4bit add_4bit_10 (.A({3'b000, c3}), .B({3'b000, c4}), .ADD4(add_4bit_10_add4));  // open: addOrSub
  Add_4bit add_4bit_11 (.A({3'b000, c5}), .B({3'b000, c6}), .ADD4(add_4bit_11_add4));  // open: addOrSub
  Add_4bit add_4bit_12 (.A({3'b000, c7}), .B({3'b000, c8}), .ADD4(add_4bit_12_add4));  // open: addOrSub
  Comparator #(.mode("unsigned"), .width(4)) comparator_9 (.a(a8), .b(B), .lt(comparator_9_lt));  // open: gt, eq
  not not_9 (c9, comparator_9_lt);
  Comparator #(.mode("unsigned"), .width(4)) comparator_10 (.a(a9), .b(B), .lt(comparator_10_lt));  // open: gt, eq
  not not_10 (c10, comparator_10_lt);
  Comparator #(.mode("unsigned"), .width(4)) comparator_11 (.a(a10), .b(B), .lt(comparator_11_lt));  // open: gt, eq
  not not_11 (c11, comparator_11_lt);
  Comparator #(.mode("unsigned"), .width(4)) comparator_12 (.a(a11), .b(B), .lt(comparator_12_lt));  // open: gt, eq
  not not_12 (c12, comparator_12_lt);
  Comparator #(.mode("unsigned"), .width(4)) comparator_13 (.a(a12), .b(B), .lt(comparator_13_lt));  // open: gt, eq
  not not_13 (c13, comparator_13_lt);
  Comparator #(.mode("unsigned"), .width(4)) comparator_14 (.a(a13), .b(B), .lt(comparator_14_lt));  // open: gt, eq
  not not_14 (c14, comparator_14_lt);
  Comparator #(.mode("unsigned"), .width(4)) comparator_15 (.a(a14), .b(B), .lt(comparator_15_lt));  // open: gt, eq
  not not_15 (c15, comparator_15_lt);
  Comparator #(.mode("unsigned"), .width(4)) comparator_16 (.a(a15), .b(B), .lt(comparator_16_lt));  // open: gt, eq
  not not_16 (not_16_out, comparator_16_lt);
  Add_4bit add_4bit_13 (.A(add_4bit_9_add4), .B(add_4bit_10_add4), .ADD4(add_4bit_13_add4));  // open: addOrSub
  Add_4bit add_4bit_14 (.A(add_4bit_11_add4), .B(add_4bit_12_add4), .ADD4(add_4bit_14_add4));  // open: addOrSub
  assign bit_extender_9_out = {{3{c9}}, c9};  // Bit_Extender bit_extender_9
  Add_4bit add_4bit_15 (.A(a8), .addOrSub(1'b1), .B(B), .ADD4(add_4bit_15_add4));
  assign bit_extender_10_out = {{3{c10}}, c10};  // Bit_Extender bit_extender_10
  Add_4bit add_4bit_16 (.A(a9), .addOrSub(1'b1), .B(B), .ADD4(add_4bit_16_add4));
  assign bit_extender_11_out = {{3{c11}}, c11};  // Bit_Extender bit_extender_11
  Add_4bit add_4bit_17 (.A(a10), .addOrSub(1'b1), .B(B), .ADD4(add_4bit_17_add4));
  assign bit_extender_12_out = {{3{c12}}, c12};  // Bit_Extender bit_extender_12
  Add_4bit add_4bit_18 (.A(a11), .addOrSub(1'b1), .B(B), .ADD4(add_4bit_18_add4));
  assign bit_extender_13_out = {{3{c13}}, c13};  // Bit_Extender bit_extender_13
  Add_4bit add_4bit_19 (.A(a12), .addOrSub(1'b1), .B(B), .ADD4(add_4bit_19_add4));
  assign bit_extender_14_out = {{3{c14}}, c14};  // Bit_Extender bit_extender_14
  Add_4bit add_4bit_20 (.A(a13), .addOrSub(1'b1), .B(B), .ADD4(add_4bit_20_add4));
  assign bit_extender_15_out = {{3{c15}}, c15};  // Bit_Extender bit_extender_15
  Add_4bit add_4bit_21 (.A(a14), .addOrSub(1'b1), .B(B), .ADD4(add_4bit_21_add4));
  assign bit_extender_16_out = {{3{not_16_out}}, not_16_out};  // Bit_Extender bit_extender_16
  Add_4bit add_4bit_22 (.A(a15), .addOrSub(1'b1), .B(B), .ADD4(add_4bit_22_add4));
  assign a9 = bit_extender_9_out & add_4bit_15_add4;  // AND_Gate and_9, 4 bits wide
  assign a10 = bit_extender_10_out & add_4bit_16_add4;  // AND_Gate and_10, 4 bits wide
  assign a11 = bit_extender_11_out & add_4bit_17_add4;  // AND_Gate and_11, 4 bits wide
  assign a12 = bit_extender_12_out & add_4bit_18_add4;  // AND_Gate and_12, 4 bits wide
  assign a13 = bit_extender_13_out & add_4bit_19_add4;  // AND_Gate and_13, 4 bits wide
  assign a14 = bit_extender_14_out & add_4bit_20_add4;  // AND_Gate and_14, 4 bits wide
  assign a15 = bit_extender_15_out & add_4bit_21_add4;  // AND_Gate and_15, 4 bits wide
  Comparator #(.mode("unsigned"), .width(4)) comparator_17 (
    .a(4'b0000), .b(and_16_out), .eq(comparator_17_eq));  // open: gt, lt
  assign and_16_out = bit_extender_16_out & add_4bit_22_add4;  // AND_Gate and_16, 4 bits wide
  Add_4bit add_4bit_23 (.A(add_4bit_24_add4), .B(add_4bit_25_add4), .ADD4(add_4bit_23_add4));  // open: addOrSub
  Add_4bit add_4bit_24 (.A(add_4bit_13_add4), .B(add_4bit_14_add4), .ADD4(add_4bit_24_add4));  // open: addOrSub
  // Probe on A
  // Probe on B
  Multiplexer #(.width(4)) multiplexer_1 (.in1(add_4bit_23_add4), .out(F), .sel(comparator_17_eq));  // open: in0
  Add_4bit add_4bit_25 (.A(add_4bit_27_add4), .B(add_4bit_26_add4), .ADD4(add_4bit_25_add4));  // open: addOrSub
  // Probe on F
  Add_4bit add_4bit_26 (.A(add_4bit_29_add4), .B(add_4bit_28_add4), .ADD4(add_4bit_26_add4));  // open: addOrSub
  Add_4bit add_4bit_27 (.A(add_4bit_31_add4), .B(add_4bit_30_add4), .ADD4(add_4bit_27_add4));  // open: addOrSub
  Add_4bit add_4bit_28 (.A({3'b000, c10}), .B({3'b000, c9}), .ADD4(add_4bit_28_add4));  // open: addOrSub
  Add_4bit add_4bit_29 (.A({3'b000, c12}), .B({3'b000, c11}), .ADD4(add_4bit_29_add4));  // open: addOrSub
  Add_4bit add_4bit_30 (.A({3'b000, c14}), .B({3'b000, c13}), .ADD4(add_4bit_30_add4));  // open: addOrSub
  Add_4bit add_4bit_31 (.A(4'b0000), .B({3'b000, c15}), .ADD4(add_4bit_31_add4));  // open: addOrSub
endmodule

module exponent (
  input  [3:0] A,
  input  [3:0] B,
  output [3:0] F
);

  wire c1, c2, c3, c4, c5, c6, c7, c8, c9, c10, c11, c12, c13, c14, c15, comparator_1_lt, comparator_2_lt,
       comparator_3_lt, comparator_4_lt, comparator_5_lt, comparator_6_lt, comparator_7_lt, comparator_8_lt,
       comparator_9_lt, comparator_10_lt, comparator_11_lt, comparator_12_lt, comparator_13_lt,
       comparator_14_lt, comparator_15_lt;
  wire [3:0] a1, a2, a3, a4, a5, a6, a7, a8, a9, a10, a11, a12, a13, a14, a15, a_t, add_4bit_2_add4,
       add_4bit_3_add4, add_4bit_4_add4, add_4bit_5_add4, add_4bit_6_add4, add_4bit_7_add4, add_4bit_8_add4,
       add_4bit_9_add4, add_4bit_10_add4, add_4bit_11_add4, add_4bit_12_add4, add_4bit_13_add4,
       add_4bit_14_add4, add_4bit_15_add4, add_4bit_16_add4, add_4bit_17_add4, add_4bit_18_add4,
       add_4bit_19_add4, add_4bit_20_add4, add_4bit_21_add4, add_4bit_22_add4, add_4bit_24_add4,
       add_4bit_25_add4, add_4bit_26_add4, add_4bit_27_add4, add_4bit_28_add4, add_4bit_29_add4,
       add_4bit_30_add4, add_4bit_31_add4, bit_extender_1_out, bit_extender_2_out, bit_extender_3_out,
       bit_extender_4_out, bit_extender_5_out, bit_extender_6_out, bit_extender_7_out, bit_extender_8_out,
       bit_extender_9_out, bit_extender_10_out, bit_extender_11_out, bit_extender_12_out,
       bit_extender_13_out, bit_extender_14_out, bit_extender_15_out, mult_1_f, mult_2_f, mult_3_f, mult_4_f,
       mult_5_f, mult_6_f, mult_7_f, mult_8_f, mult_9_f, mult_10_f, mult_11_f, mult_12_f, mult_13_f,
       mult_14_f, mult_15_f, multiplexer_1_out, multiplexer_2_out, multiplexer_3_out, multiplexer_4_out,
       multiplexer_5_out, multiplexer_6_out, multiplexer_7_out, multiplexer_8_out, multiplexer_9_out,
       multiplexer_10_out, multiplexer_11_out, multiplexer_12_out, multiplexer_13_out, multiplexer_14_out,
       multiplexer_15_out;

  Add_4bit add_4bit_1 (.A(B), .addOrSub(1'b1), .B(4'b0001), .ADD4(a_t));
  Multiplexer #(.width(4)) multiplexer_1 (.in0(4'b0000), .in1(A), .out(multiplexer_1_out), .sel(c1));
  Multiplexer #(.width(4)) multiplexer_2 (.in0(4'b0000), .in1(A), .out(multiplexer_2_out), .sel(c2));
  Multiplexer #(.width(4)) multiplexer_3 (.in0(4'b0000), .in1(A), .out(multiplexer_3_out), .sel(c3));
  Multiplexer #(.width(4)) multiplexer_4 (.in0(4'b0000), .in1(A), .out(multiplexer_4_out), .sel(c4));
  Multiplexer #(.width(4)) multiplexer_5 (.in0(4'b0000), .in1(A), .out(multiplexer_5_out), .sel(c5));
  Multiplexer #(.width(4)) multiplexer_6 (.in0(4'b0000), .in1(A), .out(multiplexer_6_out), .sel(c6));
  Multiplexer #(.width(4)) multiplexer_7 (.in0(4'b0000), .in1(A), .out(multiplexer_7_out), .sel(c7));
  Multiplexer #(.width(4)) multiplexer_8 (.in0(4'b0000), .in1(A), .out(multiplexer_8_out), .sel(c8));
  Comparator #(.mode("unsigned"), .width(4)) comparator_1 (.a(a_t), .b(4'b0001), .lt(comparator_1_lt));  // open: gt, eq
  not not_1 (c1, comparator_1_lt);
  Comparator #(.mode("unsigned"), .width(4)) comparator_2 (.a(a1), .b(4'b0001), .lt(comparator_2_lt));  // open: gt, eq
  not not_2 (c2, comparator_2_lt);
  Comparator #(.mode("unsigned"), .width(4)) comparator_3 (.a(a2), .b(4'b0001), .lt(comparator_3_lt));  // open: gt, eq
  not not_3 (c3, comparator_3_lt);
  Comparator #(.mode("unsigned"), .width(4)) comparator_4 (.a(a3), .b(4'b0001), .lt(comparator_4_lt));  // open: gt, eq
  not not_4 (c4, comparator_4_lt);
  Comparator #(.mode("unsigned"), .width(4)) comparator_5 (.a(a4), .b(4'b0001), .lt(comparator_5_lt));  // open: gt, eq
  not not_5 (c5, comparator_5_lt);
  Comparator #(.mode("unsigned"), .width(4)) comparator_6 (.a(a5), .b(4'b0001), .lt(comparator_6_lt));  // open: gt, eq
  not not_6 (c6, comparator_6_lt);
  Comparator #(.mode("unsigned"), .width(4)) comparator_7 (.a(a6), .b(4'b0001), .lt(comparator_7_lt));  // open: gt, eq
  not not_7 (c7, comparator_7_lt);
  Comparator #(.mode("unsigned"), .width(4)) comparator_8 (.a(a7), .b(4'b0001), .lt(comparator_8_lt));  // open: gt, eq
  not not_8 (c8, comparator_8_lt);
  assign bit_extender_1_out = {{3{c1}}, c1};  // Bit_Extender bit_extender_1
  Add_4bit add_4bit_2 (.A(a_t), .addOrSub(1'b1), .B(4'b0001), .ADD4(add_4bit_2_add4));
  assign bit_extender_2_out = {{3{c2}}, c2};  // Bit_Extender bit_extender_2
  Add_4bit add_4bit_3 (.A(a1), .addOrSub(1'b1), .B(4'b0001), .ADD4(add_4bit_3_add4));
  assign bit_extender_3_out = {{3{c3}}, c3};  // Bit_Extender bit_extender_3
  Add_4bit add_4bit_4 (.A(a2), .addOrSub(1'b1), .B(4'b0001), .ADD4(add_4bit_4_add4));
  assign bit_extender_4_out = {{3{c4}}, c4};  // Bit_Extender bit_extender_4
  Add_4bit add_4bit_5 (.A(a3), .addOrSub(1'b1), .B(4'b0001), .ADD4(add_4bit_5_add4));
  assign bit_extender_5_out = {{3{c5}}, c5};  // Bit_Extender bit_extender_5
  Add_4bit add_4bit_6 (.A(a4), .addOrSub(1'b1), .B(4'b0001), .ADD4(add_4bit_6_add4));
  assign bit_extender_6_out = {{3{c6}}, c6};  // Bit_Extender bit_extender_6
  Add_4bit add_4bit_7 (.A(a5), .addOrSub(1'b1), .B(4'b0001), .ADD4(add_4bit_7_add4));
  assign bit_extender_7_out = {{3{c7}}, c7};  // Bit_Extender bit_extender_7
  Add_4bit add_4bit_8 (.A(a6), .addOrSub(1'b1), .B(4'b0001), .ADD4(add_4bit_8_add4));
  assign bit_extender_8_out = {{3{c8}}, c8};  // Bit_Extender bit_extender_8
  Add_4bit add_4bit_9 (.A(a7), .addOrSub(1'b1), .B(4'b0001), .ADD4(add_4bit_9_add4));
  MULT mult_1 (.A(multiplexer_1_out), .B(multiplexer_1_out), .F(mult_1_f));
  MULT mult_2 (.A(multiplexer_2_out), .B(multiplexer_2_out), .F(mult_2_f));
  MULT mult_3 (.A(multiplexer_3_out), .B(multiplexer_3_out), .F(mult_3_f));
  MULT mult_4 (.A(multiplexer_4_out), .B(multiplexer_4_out), .F(mult_4_f));
  MULT mult_5 (.A(multiplexer_5_out), .B(multiplexer_5_out), .F(mult_5_f));
  MULT mult_6 (.A(multiplexer_6_out), .B(multiplexer_6_out), .F(mult_6_f));
  MULT mult_7 (.A(multiplexer_7_out), .B(multiplexer_7_out), .F(mult_7_f));
  MULT mult_8 (.A(multiplexer_8_out), .B(multiplexer_8_out), .F(mult_8_f));
  assign a1 = bit_extender_1_out & add_4bit_2_add4;  // AND_Gate and_1, 4 bits wide
  assign a2 = bit_extender_2_out & add_4bit_3_add4;  // AND_Gate and_2, 4 bits wide
  assign a3 = bit_extender_3_out & add_4bit_4_add4;  // AND_Gate and_3, 4 bits wide
  assign a4 = bit_extender_4_out & add_4bit_5_add4;  // AND_Gate and_4, 4 bits wide
  assign a5 = bit_extender_5_out & add_4bit_6_add4;  // AND_Gate and_5, 4 bits wide
  assign a6 = bit_extender_6_out & add_4bit_7_add4;  // AND_Gate and_6, 4 bits wide
  assign a7 = bit_extender_7_out & add_4bit_8_add4;  // AND_Gate and_7, 4 bits wide
  assign a8 = bit_extender_8_out & add_4bit_9_add4;  // AND_Gate and_8, 4 bits wide
  Comparator #(.mode("unsigned"), .width(4)) comparator_9 (.a(a8), .b(4'b0001), .lt(comparator_9_lt));  // open: gt, eq
  Comparator #(.mode("unsigned"), .width(4)) comparator_10 (
    .a(a9), .b(4'b0001), .lt(comparator_10_lt));  // open: gt, eq
  Comparator #(.mode("unsigned"), .width(4)) comparator_11 (
    .a(a10), .b(4'b0001), .lt(comparator_11_lt));  // open: gt, eq
  Comparator #(.mode("unsigned"), .width(4)) comparator_12 (
    .a(a11), .b(4'b0001), .lt(comparator_12_lt));  // open: gt, eq
  Comparator #(.mode("unsigned"), .width(4)) comparator_13 (
    .a(a12), .b(4'b0001), .lt(comparator_13_lt));  // open: gt, eq
  Comparator #(.mode("unsigned"), .width(4)) comparator_14 (
    .a(a13), .b(4'b0001), .lt(comparator_14_lt));  // open: gt, eq
  Comparator #(.mode("unsigned"), .width(4)) comparator_15 (
    .a(a14), .b(4'b0001), .lt(comparator_15_lt));  // open: gt, eq
  not not_9 (c9, comparator_9_lt);
  not not_10 (c10, comparator_10_lt);
  not not_11 (c11, comparator_11_lt);
  not not_12 (c12, comparator_12_lt);
  not not_13 (c13, comparator_13_lt);
  not not_14 (c14, comparator_14_lt);
  not not_15 (c15, comparator_15_lt);
  Add_4bit add_4bit_10 (.A(mult_1_f), .B(mult_2_f), .ADD4(add_4bit_10_add4));  // open: addOrSub
  Add_4bit add_4bit_11 (.A(mult_3_f), .B(mult_4_f), .ADD4(add_4bit_11_add4));  // open: addOrSub
  Add_4bit add_4bit_12 (.A(mult_5_f), .B(mult_6_f), .ADD4(add_4bit_12_add4));  // open: addOrSub
  Add_4bit add_4bit_13 (.A(mult_7_f), .B(mult_8_f), .ADD4(add_4bit_13_add4));  // open: addOrSub
  assign bit_extender_9_out = {{3{c9}}, c9};  // Bit_Extender bit_extender_9
  assign a9 = bit_extender_9_out & add_4bit_14_add4;  // AND_Gate and_9, 4 bits wide
  Add_4bit add_4bit_14 (.A(a8), .addOrSub(1'b1), .B(4'b0001), .ADD4(add_4bit_14_add4));
  assign bit_extender_10_out = {{3{c10}}, c10};  // Bit_Extender bit_extender_10
  assign a10 = bit_extender_10_out & add_4bit_15_add4;  // AND_Gate and_10, 4 bits wide
  Add_4bit add_4bit_15 (.A(a9), .addOrSub(1'b1), .B(4'b0001), .ADD4(add_4bit_15_add4));
  assign bit_extender_11_out = {{3{c11}}, c11};  // Bit_Extender bit_extender_11
  assign a11 = bit_extender_11_out & add_4bit_16_add4;  // AND_Gate and_11, 4 bits wide
  Add_4bit add_4bit_16 (.A(a10), .addOrSub(1'b1), .B(4'b0001), .ADD4(add_4bit_16_add4));
  assign bit_extender_12_out = {{3{c12}}, c12};  // Bit_Extender bit_extender_12
  assign a12 = bit_extender_12_out & add_4bit_17_add4;  // AND_Gate and_12, 4 bits wide
  Add_4bit add_4bit_17 (.A(a11), .addOrSub(1'b1), .B(4'b0001), .ADD4(add_4bit_17_add4));
  assign bit_extender_13_out = {{3{c13}}, c13};  // Bit_Extender bit_extender_13
  assign a13 = bit_extender_13_out & add_4bit_18_add4;  // AND_Gate and_13, 4 bits wide
  Add_4bit add_4bit_18 (.A(a12), .addOrSub(1'b1), .B(4'b0001), .ADD4(add_4bit_18_add4));
  assign bit_extender_14_out = {{3{c14}}, c14};  // Bit_Extender bit_extender_14
  assign a14 = bit_extender_14_out & add_4bit_19_add4;  // AND_Gate and_14, 4 bits wide
  Add_4bit add_4bit_19 (.A(a13), .addOrSub(1'b1), .B(4'b0001), .ADD4(add_4bit_19_add4));
  assign bit_extender_15_out = {{3{c15}}, c15};  // Bit_Extender bit_extender_15
  assign a15 = bit_extender_15_out & add_4bit_20_add4;  // AND_Gate and_15, 4 bits wide
  Add_4bit add_4bit_20 (.A(a14), .addOrSub(1'b1), .B(4'b0001), .ADD4(add_4bit_20_add4));
  // Probe on 4'b0001
  // Probe on a_t
  Add_4bit add_4bit_21 (.A(add_4bit_10_add4), .B(add_4bit_11_add4), .ADD4(add_4bit_21_add4));  // open: addOrSub
  Add_4bit add_4bit_22 (.A(add_4bit_12_add4), .B(add_4bit_13_add4), .ADD4(add_4bit_22_add4));  // open: addOrSub
  // Probe on F
  // Probe on F
  Add_4bit add_4bit_23 (.A(add_4bit_24_add4), .B(add_4bit_25_add4), .ADD4(F));  // open: addOrSub
  Add_4bit add_4bit_24 (.A(add_4bit_21_add4), .B(add_4bit_22_add4), .ADD4(add_4bit_24_add4));  // open: addOrSub
  Add_4bit add_4bit_25 (.A(add_4bit_27_add4), .B(add_4bit_26_add4), .ADD4(add_4bit_25_add4));  // open: addOrSub
  Add_4bit add_4bit_26 (.A(add_4bit_29_add4), .B(add_4bit_28_add4), .ADD4(add_4bit_26_add4));  // open: addOrSub
  Add_4bit add_4bit_27 (.A(add_4bit_31_add4), .B(add_4bit_30_add4), .ADD4(add_4bit_27_add4));  // open: addOrSub
  Add_4bit add_4bit_28 (.A(mult_10_f), .B(mult_9_f), .ADD4(add_4bit_28_add4));  // open: addOrSub
  Add_4bit add_4bit_29 (.A(mult_12_f), .B(mult_11_f), .ADD4(add_4bit_29_add4));  // open: addOrSub
  Add_4bit add_4bit_30 (.A(mult_14_f), .B(mult_13_f), .ADD4(add_4bit_30_add4));  // open: addOrSub
  Add_4bit add_4bit_31 (.A(4'b0000), .B(mult_15_f), .ADD4(add_4bit_31_add4));  // open: addOrSub
  MULT mult_9 (.A(multiplexer_9_out), .B(multiplexer_9_out), .F(mult_9_f));
  MULT mult_10 (.A(multiplexer_10_out), .B(multiplexer_10_out), .F(mult_10_f));
  MULT mult_11 (.A(multiplexer_11_out), .B(multiplexer_11_out), .F(mult_11_f));
  MULT mult_12 (.A(multiplexer_12_out), .B(multiplexer_12_out), .F(mult_12_f));
  MULT mult_13 (.A(multiplexer_13_out), .B(multiplexer_13_out), .F(mult_13_f));
  MULT mult_14 (.A(multiplexer_14_out), .B(multiplexer_14_out), .F(mult_14_f));
  MULT mult_15 (.A(multiplexer_15_out), .B(multiplexer_15_out), .F(mult_15_f));
  Multiplexer #(.width(4)) multiplexer_9 (.in0(4'b0000), .in1(A), .out(multiplexer_9_out), .sel(c9));
  Multiplexer #(.width(4)) multiplexer_10 (.in0(4'b0000), .in1(A), .out(multiplexer_10_out), .sel(c10));
  Multiplexer #(.width(4)) multiplexer_11 (.in0(4'b0000), .in1(A), .out(multiplexer_11_out), .sel(c11));
  Multiplexer #(.width(4)) multiplexer_12 (.in0(4'b0000), .in1(A), .out(multiplexer_12_out), .sel(c12));
  Multiplexer #(.width(4)) multiplexer_13 (.in0(4'b0000), .in1(A), .out(multiplexer_13_out), .sel(c13));
  Multiplexer #(.width(4)) multiplexer_14 (.in0(4'b0000), .in1(A), .out(multiplexer_14_out), .sel(c14));
  Multiplexer #(.width(4)) multiplexer_15 (.in0(4'b0000), .in1(A), .out(multiplexer_15_out), .sel(c15));

  // Other names for the same wires on the sheet: by[3:0] = A
endmodule
